# Fritzing sketch Address Selector (saved by Fritzing 0.9.4)
circuit board: 0.969322cm x 1.33338cm
breadboards: 1

parts:
  MISO/Vcc = female pin header, 2 pins [form="♀ (female)"]
  SCK/MOSI = female pin header, 2 pins [form="♀ (female)"]
  Reset/Gnd = female pin header, 2 pins [form="♀ (female)"]
  J1 = female pin header, 2 pins [form="♀ (female)"]
  J2 = female pin header, 2 pins [form="♀ (female)"]
  J3 = female pin header, 2 pins [form="♀ (female)"]

nets:
  N1: MISO/Vcc.pin1, J1.pin2
  N2: SCK/MOSI.pin1, J2.pin1
  N3: SCK/MOSI.pin2, J3.pin1
  N4: Reset/Gnd.pin1, J1.pin1, J2.pin2, J3.pin2

notes:
  A0
  A1
  A2
